// Logisim project bfcpu.circ as structural Verilog: 5 circuits, main circuit main
module main (
);

  wire and_1_out, button_1_out, button_2_out, controllersim_1_art_par, controllersim_1_halted,
       controllersim_1_rclk, controllersim_1_wclk, demultiplexer_1_out0, demultiplexer_1_out1,
       demultiplexer_1_out2, demultiplexer_1_out3, not_1_out, or_1_out;
  wire [1:0] controllersim_1_opnd, controllersim_1_opr;
  wire [6:0] keyboard_1_data;
  wire [7:0] alu_1_res, alu_1_res_2, controlled_buffer_2_out, controllersim_1_counter, controllersim_1_cycle,
       ram_1_data, rom_1_data;
  wire [15:0] alu_1_tsto_out, DP_q, multiplexer_1_out, PC_q;

  Button button_1 (.out(button_1_out));
  Keyboard #(.buflen(32), .trigger("rising")) keyboard_1 (
    .clk(button_1_out), .data(keyboard_1_data));  // open: re, clr, avail
  Button button_2 (.out(button_2_out));
  Register #(.width(16), .trigger("rising")) PC (
    .D({alu_1_res_2, alu_1_res}), .Q(PC_q), .clk(demultiplexer_1_out1));  // open: en, clr
  // Probe on {{9{1'b0}}, keyboard_1_data}
  ROM #(.addrWidth(16), .dataWidth(8)) rom_1 (.addr(PC_q), .data(rom_1_data));  // open: sel
  Demultiplexer #(.select(2), .width(1), .tristate("false")) demultiplexer_1 (
    .out0(demultiplexer_1_out0), .out1(demultiplexer_1_out1), .out2(demultiplexer_1_out2),
    .out3(demultiplexer_1_out3), .in(controllersim_1_wclk), .sel(controllersim_1_opnd));
  // Probe on rom_1_data
  // Probe on button_1_out
  or or_1 (or_1_out, demultiplexer_1_out0, demultiplexer_1_out3);
  // Probe on controllersim_1_rclk
  // Probe on controllersim_1_wclk
  ControllerSim controllersim_1 (
    .Opcode(rom_1_data), .Halt(button_1_out), .START(button_2_out), .WCLK(controllersim_1_wclk),
    .RCLK(controllersim_1_rclk), .Halted(controllersim_1_halted), .Counter(controllersim_1_counter),
    .Cycle(controllersim_1_cycle), .OPND(controllersim_1_opnd), .OPR(controllersim_1_opr),
    .ART_PAR(controllersim_1_art_par));
  // Probe on controllersim_1_cycle
  // Probe on controllersim_1_counter
  LED #(.active("true")) Halted (.in(controllersim_1_halted));
  Register #(.width(16), .trigger("rising")) DP (
    .D({alu_1_res_2, alu_1_res}), .Q(DP_q), .clk(demultiplexer_1_out2));  // open: en, clr
  // Probe on controllersim_1_opnd
  and and_1 (and_1_out, or_1_out, controllersim_1_wclk);
  not not_1 (not_1_out, and_1_out);
  // Probe on alu_1_tsto_out
  // Probe on multiplexer_1_out
  Multiplexer #(.select(2), .width(16)) multiplexer_1 (
    .in0({{9{1'b0}}, keyboard_1_data}), .in1(PC_q), .in2(DP_q), .in3({{8{1'b0}}, controlled_buffer_2_out}),
    .out(multiplexer_1_out), .sel(controllersim_1_opnd));
  // Probe on controllersim_1_art_par
  RAM #(.addrWidth(16), .dataWidth(8), .bus("asynch")) ram_1 (
    .addr(DP_q), .data(ram_1_data), .ld(not_1_out));  // open: sel, clr
  assign ram_1_data = and_1_out ? alu_1_res : 8'bz;  // Controlled_Buffer controlled_buffer_1
  assign controlled_buffer_2_out = not_1_out ? ram_1_data : 8'bz;  // Controlled_Buffer controlled_buffer_2
  // Probe on controlled_buffer_2_out
  ALU alu_1 (
    .PAR(multiplexer_1_out), .ART_PAR(controllersim_1_art_par), .OP(controllersim_1_opr),
    .TSTO_OUT(alu_1_tsto_out), .clk(controllersim_1_rclk), .RES({alu_1_res_2, alu_1_res}));  // open: NZ
  // Probe on {alu_1_res_2, alu_1_res}

  // Notes on the sheet:
  //   INPUT DRIVER
  //   PROGRAM ROM
  //   contents of rom_1 (hex, n*v repeats v):
  //   2b 3e 2d 3c 2d 3e 2b
  //   CONTROL UNIT
  //   DATA RAM
endmodule

module ALU (
  input  [15:0] PAR,
  input  ART_PAR,
  input  [1:0] OP,
  input  clk,
  output [15:0] TSTO_OUT,
  output NZ,
  output [15:0] RES
);

  wire adder_1_cout, adder_2_cout, adder_3_cout, or_1_out, or_2_out;
  wire [3:0] adder_1_out, adder_2_out, adder_3_out, adder_4_out;

  or or_1 (or_1_out, 1'b0, PAR[0], PAR[1], PAR[2], PAR[3], PAR[4], PAR[5], PAR[6], PAR[7]);
  or or_2 (or_2_out, 1'b0, PAR[8], PAR[9], PAR[10], PAR[11], PAR[12], PAR[13], PAR[14], PAR[15]);
  or or_3 (NZ, or_1_out, or_2_out);
  Adder #(.width(4)) adder_1 (
    .a(PAR[3:0]), .b({{3{ART_PAR}}, 1'b1}), .out(adder_1_out), .cin(1'b0), .cout(adder_1_cout));
  Adder #(.width(4)) adder_2 (
    .a(PAR[7:4]), .b({4{ART_PAR}}), .out(adder_2_out), .cin(adder_1_cout), .cout(adder_2_cout));
  Adder #(.width(4)) adder_3 (
    .a(PAR[11:8]), .b({4{ART_PAR}}), .out(adder_3_out), .cin(adder_2_cout), .cout(adder_3_cout));
  Adder #(.width(4)) adder_4 (.a(PAR[15:12]), .b({4{ART_PAR}}), .out(adder_4_out), .cin(adder_3_cout));  // open: cout
  Multiplexer #(.select(2), .width(16)) multiplexer_1 (
    .in0(PAR), .in1({adder_4_out, adder_3_out, adder_2_out, adder_1_out}), .in2({PAR[7:0], PAR[15:8]}),
    .in3({RES[15:8], PAR[7:0]}), .out(TSTO_OUT), .sel(OP));
  Register #(.width(16), .trigger("rising")) BUF (.D(TSTO_OUT), .Q(RES), .clk(clk));  // open: en, clr

  // Notes on the sheet:
  //   NZ
  //   NOP
  //   ART
  //   SWP
  //   LOW
  //   ART
  //   SWP
  //   LOW
  //   NOP
  //   LOW
endmodule

module xx (
  input  [7:0] D,
  input  en,
  input  clk,
  output [7:0] Q
);

  wire [7:0] multiplexer_1_out;

  Multiplexer #(.select(1), .width(8)) multiplexer_1 (.in0(Q), .in1(D), .out(multiplexer_1_out), .sel(en));
  Register #(.width(8), .trigger("rising")) register_1 (.D(multiplexer_1_out), .Q(Q), .clk(clk));  // open: en, clr
endmodule

module Controller (
  input  [3:0] Opcode,
  input  Halt,
  output WCLK,
  output RCLK,
  output [1:0] selOperand,
  output fDec,
  output Halted,
  output [7:0] Counter,
  output [1:0] Cycle
);

  wire and_1_out, and_2_out, and_3_out, clock_1_out, d_ff_1_qn, decoder_1_out0, decoder_1_out1,
       decoder_2_out0, demultiplexer_1_out0, demultiplexer_1_out1, multiplexer_1_out, not_1_out, not_2_out,
       not_3_out, not_4_out, or_1_out, t_ff_1_qn, xnor_1_out;
  wire [2:2] multiplexer_2_out;

  T_Flip_Flop #(.trigger("rising")) t_ff_1 (
    .clk(multiplexer_1_out), .T(1'b1), .Q(Halted), .Qn(t_ff_1_qn));  // open: preset, reset, en
  Multiplexer #(.select(1), .width(1)) multiplexer_1 (
    .in0(decoder_2_out0), .in1(Halt), .out(multiplexer_1_out), .sel(Halted));
  Clock #(.highDuration(1), .lowDuration(1)) clock_1 (.out(clock_1_out));
  and and_1 (and_1_out, clock_1_out, t_ff_1_qn);
  not not_1 (not_1_out, clock_1_out);
  and and_2 (and_2_out, decoder_2_out0, not_2_out);
  not not_2 (not_2_out, and_3_out);
  and and_3 (and_3_out, or_1_out, not_3_out);
  not not_3 (not_3_out, d_ff_1_qn);
  D_Flip_Flop #(.trigger("rising")) d_ff_1 (
    .clk(not_1_out), .D(and_2_out), .Qn(d_ff_1_qn));  // open: Q, preset, en, reset
  Demultiplexer #(.select(1), .width(1), .tristate("false")) demultiplexer_1 (
    .out0(demultiplexer_1_out0), .out1(demultiplexer_1_out1), .in(and_1_out), .sel(d_ff_1_qn));
  not not_4 (not_4_out, or_1_out);
  or or_1 (or_1_out, demultiplexer_1_out0, demultiplexer_1_out1);
  Counter #(.width(2), .max('h3), .ongoal("wrap"), .trigger("rising")) counter_1 (
    .Q(Cycle), .clk(demultiplexer_1_out1));  // open: load, D, count, carry, clr
  and and_4 (WCLK, not_4_out, decoder_1_out0);
  and and_5 (RCLK, not_4_out, decoder_1_out1);
  Decoder #(.select(1), .tristate("false")) decoder_1 (.out0(decoder_1_out0), .out1(decoder_1_out1), .sel(Cycle[0]));
  xnor xnor_1 (xnor_1_out, Cycle[0], Cycle[1]);
  Multiplexer #(.select(1), .width(4)) multiplexer_2 (
    .in0(Opcode), .in1(4'b0001), .out({fDec, multiplexer_2_out[2], selOperand}), .sel(xnor_1_out));
  Decoder #(.select(2), .tristate("false")) decoder_2 (
    .out0(decoder_2_out0), .sel(selOperand));  // open: out1, out2, out3
  // Probe on selOperand
  Counter #(.width(8), .max('hff), .ongoal("wrap"), .trigger("rising")) counter_2 (
    .Q(Counter), .clk(demultiplexer_1_out1));  // open: load, D, count, carry, clr
endmodule

module ControllerSim (
  input  [7:0] Opcode,
  input  Halt,
  input  START,
  output WCLK,
  output RCLK,
  output [1:0] OPND,
  output [1:0] OPR,
  output ART_PAR,
  output [7:0] Counter,
  output [7:0] Cycle,
  output Halted
);

  wire clock_1_out, d_ff_1_q, not_1_out, or_1_out;
  wire [7:0] register_1_q, rom_1_data;

  Register #(.width(8), .trigger("rising")) register_1 (
    .D(Opcode), .en(1'b1), .Q(register_1_q), .clk(or_1_out));  // open: clr
  or or_1 (or_1_out, START, d_ff_1_q);
  Clock #(.highDuration(1), .lowDuration(1)) clock_1 (.out(clock_1_out));
  Counter #(.width(8), .max('hff), .ongoal("wrap"), .trigger("rising")) counter_1 (
    .Q(Cycle), .clk(clock_1_out), .clr(or_1_out));  // open: load, D, count, carry
  Counter #(.width(8), .max('hff), .ongoal("wrap"), .trigger("rising")) counter_2 (.clk(d_ff_1_q));  // open: load, D, count, Q, carry, clr
  not not_1 (not_1_out, clock_1_out);
  ROM #(.addrWidth(16), .dataWidth(8)) rom_1 (
    .addr({register_1_q, Cycle}), .data({rom_1_data[7:6], OPND, OPR, ART_PAR, rom_1_data[0]}));  // open: sel
  D_Flip_Flop #(.trigger("rising")) d_ff_1 (
    .clk(clock_1_out), .D(rom_1_data[0]), .Q(d_ff_1_q));  // open: Qn, preset, en, reset
  and and_1 (WCLK, not_1_out, rom_1_data[7]);
  and and_2 (RCLK, not_1_out, rom_1_data[6]);
  Counter #(.width(8), .max('hff), .ongoal("wrap"), .trigger("rising")) counter_3 (
    .Q(Counter), .clk(clock_1_out));  // open: load, D, count, carry, clr

  // Notes on the sheet:
  //   contents of rom_1 (hex, n*v repeats v):
  //   1 11007*0 74 80 54 91 508*0 76 80 54 91 3836*0 66 a0 54 91 508*0 64 a0 54 91
endmodule
